// Logisim project schematic.circ as structural Verilog: 3 circuits, main circuit main
module main (
  input  in_1,
  output [23:0] out_2
);

  wire and_1_out, clock_1_out, cmp_1_out_2, controlled_buffer_4_out, controlled_buffer_9_out, not_1_out,
       not_2_out, or_1_out;
  wire [1:0] counter_1_q;
  wire [7:0] not_3_out;
  wire [13:0] rom_1_data;
  wire [15:0] alu_1_out_5, controlled_buffer_1_out, controlled_buffer_2_out, controlled_buffer_3_out,
       controlled_buffer_5_out, controlled_buffer_8_out, register_1_q, register_2_q, register_3_q, undriven;
  wire [23:0] counter_2_q, rom_2_data;

  Clock clock_1 (.out(clock_1_out));
  not not_1 (not_1_out, clock_1_out);
  Counter #(.max('h4), .trigger("falling"), .width(2)) counter_1 (
    .Q(counter_1_q), .clk(not_1_out));  // open: load, D, count, carry, up, clr
  ROM #(.addrWidth(10), .dataWidth(14)) rom_1 (.addr({rom_2_data[23:16], counter_1_q}), .data(rom_1_data));
  RAM #(.addrWidth(16), .dataWidth(16)) ram_1 (
    .addr(register_1_q), .we(rom_1_data[5]), .oe(rom_1_data[6]), .clk(clock_1_out),
    .din(controlled_buffer_2_out));  // open: dout
  assign controlled_buffer_1_out = rom_1_data[4] ? controlled_buffer_3_out : 16'bz;  // Controlled_Buffer controlled_buffer_1
  Register #(.trigger("high"), .width(16)) register_1 (
    .D(controlled_buffer_1_out), .clk(rom_1_data[4]), .Q(register_1_q));  // open: en, clr
  assign controlled_buffer_2_out = rom_1_data[5] ? controlled_buffer_3_out : 16'bz;  // Controlled_Buffer controlled_buffer_2
  assign controlled_buffer_3_out = rom_1_data[6] ? undriven : 16'bz;  // Controlled_Buffer controlled_buffer_3
  assign controlled_buffer_4_out = rom_1_data[2] ? clock_1_out : 1'bz;  // Controlled_Buffer controlled_buffer_4
  assign controlled_buffer_5_out = rom_1_data[2] ? controlled_buffer_3_out : 16'bz;  // Controlled_Buffer controlled_buffer_5
  Register #(.width(16)) register_2 (
    .D(controlled_buffer_5_out), .clk(controlled_buffer_4_out), .Q(register_2_q));  // open: en, clr
  assign controlled_buffer_3_out = rom_1_data[0] ? register_2_q : 16'bz;  // Controlled_Buffer controlled_buffer_6
  assign controlled_buffer_3_out = rom_1_data[7] ? alu_1_out_5 : 16'bz;  // Controlled_Buffer controlled_buffer_7
  assign controlled_buffer_8_out = rom_1_data[3] ? controlled_buffer_3_out : 16'bz;  // Controlled_Buffer controlled_buffer_8
  assign controlled_buffer_9_out = rom_1_data[3] ? clock_1_out : 1'bz;  // Controlled_Buffer controlled_buffer_9
  Register #(.width(16)) register_3 (
    .D(controlled_buffer_8_out), .clk(controlled_buffer_9_out), .Q(register_3_q));  // open: en, clr
  not not_2 (not_2_out, rom_1_data[8]);
  assign rom_1_data[9] = rom_1_data[1] ? rom_1_data[8] : 1'bz;  // Controlled_Buffer controlled_buffer_10
  assign controlled_buffer_3_out = rom_1_data[1] ? register_3_q : 16'bz;  // Controlled_Buffer controlled_buffer_11
  assign rom_1_data[9] = rom_1_data[8] ? not_2_out : 1'bz;  // Controlled_Buffer controlled_buffer_12
  CMP cmp_1 (.in_1(register_2_q), .out_2(cmp_1_out_2));
  assign controlled_buffer_3_out = rom_1_data[10] ? rom_2_data[15:0] : 16'bz;  // Controlled_Buffer controlled_buffer_13
  assign not_3_out = ~{8{1'b1}};  // NOT_Gate not_3, 8 bits wide
  ALU alu_1 (.in_1(register_2_q), .in_2(register_3_q), .ADDSUB(rom_1_data[9]), .CLK(clock_1_out), .out_5(alu_1_out_5));
  and and_1 (and_1_out, cmp_1_out_2, in_1);
  assign out_2 = {{8{1'b0}}, rom_2_data[15:0]};  // Bit_Extender bit_extender_1
  or or_1 (or_1_out, and_1_out, rom_1_data[12]);
  Counter #(.max('hffffff), .trigger("falling"), .width(24)) counter_2 (
    .load(or_1_out), .clk(rom_1_data[11]), .D(out_2), .Q(counter_2_q));  // open: clr, up, count, carry
  ROM #(.addrWidth(24), .dataWidth(24)) rom_2 (.addr(counter_2_q), .data(rom_2_data));

  // Notes on the sheet:
  //   CE
  //   LADDR
  //   OO
  //   ALU SUB
  //   ALU ADD
  //   ALU OUT
  //   contents of rom_1 (hex, n*v repeats v):
  //   4*0 404 0 0 800 408 0 0 800 410 21 0 800 410 22 0 800 100 84 0 800 200 84 0 800 1000 0 0 800 1000 0
  //   0 2000
  //   RAM OUT
  //   RAM
  //   RAM IN
  //   MAR IN
  //   RB IN
  //   RA IN
  //   RB OUT
  //   RA OUT
  //   RA
  //   RB
  //   TOP = Operand
  //   OPERAND LINE
  //   contents of rom_2 (hex, n*v repeats v):
  //   1000a 80000
endmodule

module ALU (
  input  [15:0] in_1,
  input  [15:0] in_2,
  input  ADDSUB,
  input  CLK,
  output [15:0] out_5
);

  wire register_1_q;
  wire [15:0] adder_1_out, subtractor_1_out;

  Register #(.width(1)) register_1 (.D(ADDSUB), .clk(CLK), .Q(register_1_q));  // open: en, clr
  Adder #(.width(16)) adder_1 (.a(in_1), .b(in_2), .out(adder_1_out));  // open: cin, cout
  Subtractor #(.width(16)) subtractor_1 (.a(in_1), .b(in_2), .out(subtractor_1_out));  // open: bin, bout
  Multiplexer #(.width(16)) multiplexer_1 (.in0(adder_1_out), .in1(subtractor_1_out), .out(out_5), .sel(register_1_q));

  // Notes on the sheet:
  //   0 = ADD 1 = SUB
endmodule

module CMP (
  input  [15:0] in_1,
  output out_2
);

  wire or_1_out, or_2_out, or_3_out, or_4_out, or_5_out, or_6_out, or_7_out, or_8_out, or_9_out, or_10_out,
       or_11_out, or_12_out, or_13_out, or_14_out;

  or or_1 (or_1_out, in_1[0], in_1[1]);
  or or_2 (or_2_out, in_1[2], in_1[3]);
  or or_3 (or_3_out, in_1[4], in_1[5]);
  or or_4 (or_4_out, in_1[6], in_1[7]);
  or or_5 (or_5_out, in_1[8], in_1[9]);
  or or_6 (or_6_out, in_1[10], in_1[11]);
  or or_7 (or_7_out, in_1[12], in_1[13]);
  or or_8 (or_8_out, in_1[14], in_1[15]);
  or or_9 (or_9_out, or_1_out, or_2_out);
  or or_10 (or_10_out, or_9_out, or_11_out);
  or or_11 (or_11_out, or_3_out, or_4_out);
  or or_12 (or_12_out, or_5_out, or_6_out);
  or or_13 (or_13_out, or_12_out, or_14_out);
  or or_14 (or_14_out, or_7_out, or_8_out);
  or or_15 (out_2, or_10_out, or_13_out);
endmodule
